// Digital circuit 1-bit-adder.dig as structural Verilog
module _1_bit_adder (
  input  A,
  input  B,
  input  Carry_in,
  output Sum,
  output Carryout
);

  wire and_1_out, and_2_out, xor_1_out;

  xor xor_1 (xor_1_out, A, B);
  and and_1 (and_1_out, A, B);
  and and_2 (and_2_out, xor_1_out, Carry_in);
  xor xor_2 (Sum, xor_1_out, Carry_in);
  or or_1 (Carryout, and_2_out, and_1_out);
endmodule
