// Digital circuit 2-bit.dig as structural Verilog
module _2_bit (
  input  [1:0] A1,
  input  [1:0] A0,
  input  [1:0] B1,
  input  [1:0] B0,
  output [1:0] P0,
  output [1:0] P1,
  output [1:0] P2,
  output [1:0] P3
);

  wire [1:0] and_2_out, and_3_out, and_4_out, and_5_out, and_6_out, and_7_out;

  assign P0 = A0 & B0;  // And and_1, 2 bits wide
  assign and_2_out = A1 & B0;  // And and_2, 2 bits wide
  assign and_3_out = A0 & B1;  // And and_3, 2 bits wide
  assign and_4_out = A1 & B1;  // And and_4, 2 bits wide
  assign and_5_out = A1 & B0 & A0 & B1;  // And and_5, 2 bits wide
  assign and_6_out = A1 & B1;  // And and_6, 2 bits wide
  assign and_7_out = A0 & B0;  // And and_7, 2 bits wide
  assign P1 = and_2_out ^ and_3_out;  // XOr xor_1, 2 bits wide
  assign P2 = and_4_out ^ and_5_out;  // XOr xor_2, 2 bits wide
  assign P3 = and_6_out & and_7_out;  // And and_8, 2 bits wide
endmodule
