// Digital circuit 4-bit.new.dig as structural Verilog
module _4_bit_new (
  input  [3:0] A,
  input  [3:0] B,
  input  in_5,
  output [3:0] Sum,
  output out_4
);

  wire cin_1_p3, cin_2_p3, cin_3_p3;

  // cin cin_1: pin names not known; wires that end beside it: A[3], B[3], cin_1_p3, Sum[3], out_4
  // cin cin_2: pin names not known; wires that end beside it: A[2], B[2], cin_2_p3, Sum[2], cin_1_p3
  // cin cin_3: pin names not known; wires that end beside it: A[1], B[1], cin_3_p3, Sum[1], cin_2_p3
  // cin cin_4: pin names not known; wires that end beside it: A[0], B[0], in_5, Sum[0], cin_3_p3
endmodule
